# Fritzing sketch esp32cam (saved by Fritzing 0.9.3b)

parts:
  Part3 = Arduino Uno (Rev3)
  ESP32_-_Back1 = ESP32 - CAM

nets:
  GND: Part3.GND, ESP32_-_Back1.GND
  N1: Part3.D0/RX, ESP32_-_Back1.GPIO3_/_RX
  N2: Part3.D1/TX, ESP32_-_Back1.GPIO1_/_TX
  5V: Part3.5V, ESP32_-_Back1.5V
  N3: ESP32_-_Back1.GPIO16, ESP32_-_Back1.GPIO0

custom parts:
  ESP32 - CAM: The ESP32-CAM has a very competitive small-size camera module that can operate independently as a minimum system with a footprint of only 27*40.5*4.5mm and a deep sleep current of up to 6mA.
